// Logisim project ProjectFinalSubmit.circ as structural Verilog: 1 circuit, main circuit main
module main (
);

  wire ADD, CLK, clock_1_out, CLR, COM, comparator_1_eq, decoder_2_out0, decoder_2_out1, decoder_2_out2,
       decoder_2_out3, HLT, JMP, JMP_en, LDR, LSL, LSR, not_1_out, register_1_q, START_out, STR, SUB;
  wire [7:0] adder_1_out, counter_1_q, R1, R2, R3, R4, RAM_val, Rd, Result, Rs, shifter_1_out, shifter_2_out,
       subtractor_1_out;
  wire [15:0] Instruction;

  Decoder #(.select(4)) decoder_1 (
    .out0(LDR), .out1(STR), .out2(ADD), .out3(SUB), .out4(LSL), .out5(LSR), .out6(COM), .out7(JMP),
    .sel(Instruction[3:0]));  // open: out8, out9, out10, out11, out12, out13, out14, out15, en
  Decoder #(.select(2)) decoder_2 (
    .out0(decoder_2_out0), .out1(decoder_2_out1), .out2(decoder_2_out2), .out3(decoder_2_out3),
    .sel(Instruction[7:6]));  // open: en
  Register R0 (.D(Result), .en(decoder_2_out0), .clk(CLK), .Q(R1), .clr(CLR));
  Register u_R1 (.D(Result), .en(decoder_2_out1), .clk(CLK), .Q(R2), .clr(CLR));
  Register u_R2 (.D(Result), .en(decoder_2_out2), .clk(CLK), .Q(R3), .clr(CLR));
  Register u_R3 (.D(Result), .en(decoder_2_out3), .clk(CLK), .Q(R4), .clr(CLR));
  Adder adder_1 (.a(Rd), .b(Rs), .out(adder_1_out));  // open: cin, cout
  Subtractor subtractor_1 (.a(Rd), .b(Rs), .out(subtractor_1_out));  // open: bin, bout
  Shifter shifter_1 (.in(Rs), .\dist (3'b001), .out(shifter_1_out));
  Shifter #(.shift("lr")) shifter_2 (.in(Rs), .\dist (3'b001), .out(shifter_2_out));
  Comparator comparator_1 (.a(Rd), .b(Rs), .eq(comparator_1_eq));  // open: gt, lt
  Clock clock_1 (.out(clock_1_out));
  not not_1 (not_1_out, HLT);
  assign CLK = not_1_out ? clock_1_out : 1'bz;  // Controlled_Buffer controlled_buffer_1
  Register #(.width(1)) register_1 (.D(comparator_1_eq), .en(COM), .clk(CLK), .Q(register_1_q));  // open: clr
  Button START (.out(START_out));
  assign Result = LDR ? RAM_val : 8'bz;  // Controlled_Buffer controlled_buffer_2
  assign Result = STR ? Rs : 8'bz;  // Controlled_Buffer controlled_buffer_3
  assign Result = ADD ? adder_1_out : 8'bz;  // Controlled_Buffer controlled_buffer_4
  assign Result = SUB ? subtractor_1_out : 8'bz;  // Controlled_Buffer controlled_buffer_5
  assign Result = LSL ? shifter_1_out : 8'bz;  // Controlled_Buffer controlled_buffer_6
  assign Result = LSR ? shifter_2_out : 8'bz;  // Controlled_Buffer controlled_buffer_7
  and and_1 (JMP_en, JMP, register_1_q);
  Counter counter_1 (
    .clr(START_out), .load(JMP_en), .clk(CLK), .D(Instruction[15:8]), .Q(counter_1_q));  // open: up, count, carry
  Multiplexer #(.select(2), .width(8)) multiplexer_1 (
    .in0(R1), .in1(R2), .in2(R3), .in3(R4), .out(Rd), .sel(Instruction[7:6]));
  Multiplexer #(.select(2), .width(8)) multiplexer_2 (
    .in0(R1), .in1(R2), .in2(R3), .in3(R4), .out(Rs), .sel(Instruction[5:4]));
  ROM #(.dataWidth(16)) rom_1 (.addr(counter_1_q), .data(Instruction));
  RAM #(.trigger("falling")) ram_1 (
    .addr(Instruction[15:8]), .we(STR), .oe(LDR), .clk(CLK), .din(Result), .dout(RAM_val));
  Comparator #(.width(16)) comparator_2 (.a(Instruction), .b(16'haaaa), .eq(CLR));  // open: gt, lt
  Comparator #(.width(16)) comparator_3 (.a(Instruction), .b(16'hbbbb), .eq(HLT));  // open: gt, lt
  LED led_1 (.in(HLT));

  // Other names for the same wires on the sheet: Memory_adrs[7:0] = Instruction[15:8]; OPCODE[3:0] = Instruction[3:0];
  //   Reg_D[1:0] = Instruction[7:6]; Reg_S[1:0] = Instruction[5:4]

  // Notes on the sheet:
  //   00
  //   01
  //   10
  //   11
  //   contents of rom_1 (hex, n*v repeats v):
  //   ab80 ac00 82 ad21 aaaa bc40 bd80 96 1007 aaaa a0c0 a100 4 4 32 a101 aaaa dc80 a5 dc21 aaaa c900 ca40
  //   13 cb01 aaaa bbbb
  //   To clear register content after each program
  //   To halt the program after the last instruction
  //   Addition of two numbers
  //   LDR R2, 0xAB
  //   AB80
  //   LDR R0, 0xAC
  //   AC00
  //   ADD R2, R0
  //   0082
  //   STR  R2, 0xAD
  //   AD21
  //   1000=8
  //   1000=8
  //   0010=2
  //   Conditional jump
  //   LDR R1, 0xBC
  //   BC40
  //   LDR R2, 0xBD
  //   BD80
  //   CMP R1, R2
  //   0096
  //   JMP 0x11
  //   1007
  //   0100=4
  //   Multiplication of a number by 5
  //   LDR R3, 0xA0
  //   A0C0
  //   LDR R0, 0xA1
  //   A100
  //   LSL R0, R0
  //   0004
  //   LSL R0, R0
  //   0004
  //   ADD R0, R3
  //   0032
  //   STR R0, 0xA1
  //   A101
  //   1100=C
  //   0011=3
  //   LDR R2, 0xDC
  //   DC80
  //   LSR R2, R2
  //   00A5
  //   STR R2, 0xDC
  //   DC21
  //   Shifting a number to the right (division by 2)
  //   1000=8
  //   1010=A
  //   0010=2
  //   Subtracting a number from another
  //   LDR R0, 0xC9
  //   C900
  //   LDR R1, 0xCA
  //   CA40
  //   SUB R0, R1
  //   0013
  //   STR R0, 0xCB
  //   CB01
endmodule
